// Logisim project hw3.circ as structural Verilog: 9 circuits, main circuit main circuit
module main_circuit (
  input  [3:0] A_in,
  input  [3:0] B_in,
  input  S2,
  input  S1,
  input  S0,
  output [3:0] Output
);

  wire and_1_out, and_2_out, and_3_out, and_4_out, and_5_out, and_6_out, and_7_out, and_8_out, not_1_out,
       not_2_out, not_3_out, not_4_out, not_5_out, not_6_out, not_7_out, not_8_out, not_9_out, not_10_out,
       not_11_out, not_12_out;
  wire [3:0] and_9_out, and_10_out, and_11_out, and_12_out, and_13_out, and_14_out, and_15_out, and_16_out,
       and_17_out, comparator_1_out_3, leftshifter_1_out_2, n4bitadder_1_output,
       n4bitnegation_1_alternate_in, not_13_out, or_1_out, split_1_out, split_2_out, split_3_out,
       split_4_out, split_5_out, split_6_out, split_7_out, split_8_out, subtractor_1_out;

  not not_1 (not_1_out, S2);
  not not_2 (not_2_out, S1);
  not not_3 (not_3_out, S0);
  not not_4 (not_4_out, S2);
  not not_5 (not_5_out, S1);
  not not_6 (not_6_out, S2);
  not not_7 (not_7_out, S0);
  not not_8 (not_8_out, S2);
  not not_9 (not_9_out, S1);
  not not_10 (not_10_out, S0);
  not not_11 (not_11_out, S1);
  not not_12 (not_12_out, S0);
  and and_1 (and_1_out, not_1_out, not_2_out, not_3_out);
  and and_2 (and_2_out, not_4_out, not_5_out, S0);
  and and_3 (and_3_out, not_6_out, S1, not_7_out);
  and and_4 (and_4_out, not_8_out, S1, S0);
  and and_5 (and_5_out, S2, not_9_out, not_10_out);
  and and_6 (and_6_out, S2, not_11_out, S0);
  and and_7 (and_7_out, S2, S1, not_12_out);
  and and_8 (and_8_out, S2, S1, S0);
  Split split_1 (.In(and_1_out), .out(split_1_out));
  Split split_2 (.In(and_2_out), .out(split_2_out));
  Split split_3 (.In(and_3_out), .out(split_3_out));
  Split split_4 (.In(and_4_out), .out(split_4_out));
  Split split_5 (.In(and_5_out), .out(split_5_out));
  Split split_6 (.In(and_6_out), .out(split_6_out));
  Split split_7 (.In(and_7_out), .out(split_7_out));
  Split split_8 (.In(and_8_out), .out(split_8_out));
  _4bitAdder u_4bitadder_1 (
    .Carry_In(1'b0), .A_in(A_in), .B_in(B_in), .Output(n4bitadder_1_output));  // open: Carry_Out
  Subtractor subtractor_1 (.B_in(B_in), .A_in(A_in), .Out(subtractor_1_out));
  _4BitNegation u_4bitnegation_1 (.A_in(A_in), .Alternate_in(n4bitnegation_1_alternate_in));
  assign and_9_out = A_in & B_in;  // AND_Gate and_9, 4 bits wide
  assign or_1_out = A_in | B_in;  // OR_Gate or_1, 4 bits wide
  Comparator comparator_1 (.in_1(A_in), .in_2(B_in), .out_3(comparator_1_out_3));
  LeftShifter leftshifter_1 (.in_1(A_in), .out_2(leftshifter_1_out_2));
  assign and_10_out = split_1_out & n4bitadder_1_output;  // AND_Gate and_10, 4 bits wide
  assign and_11_out = split_2_out & subtractor_1_out;  // AND_Gate and_11, 4 bits wide
  assign and_12_out = split_3_out & n4bitnegation_1_alternate_in;  // AND_Gate and_12, 4 bits wide
  assign and_13_out = split_4_out & and_9_out;  // AND_Gate and_13, 4 bits wide
  assign and_14_out = split_5_out & or_1_out;  // AND_Gate and_14, 4 bits wide
  assign and_15_out = split_6_out & not_13_out;  // AND_Gate and_15, 4 bits wide
  assign not_13_out = ~A_in;  // NOT_Gate not_13, 4 bits wide
  assign and_16_out = split_7_out & comparator_1_out_3;  // AND_Gate and_16, 4 bits wide
  assign and_17_out = split_8_out & leftshifter_1_out_2;  // AND_Gate and_17, 4 bits wide
  assign Output = and_10_out | and_11_out | and_12_out | and_13_out | and_14_out | and_15_out | and_16_out | and_17_out;  // OR_Gate or_2, 4 bits wide

  // Notes on the sheet:
  //   Add
  //   Subtract
  //   Negate
  //   AND
  //   OR
  //   NOT
  //   ==
  //   <<1
  //   4 Bit ALU
  //   Adam Yost
endmodule

module _1bitALU (
  input  A,
  input  B,
  input  in_3,
  input  S2,
  input  S1,
  input  S0,
  output out_7
);

  wire and_1_out, and_2_out, and_3_out, and_4_out, and_5_out, and_6_out, and_7_out, and_8_out, and_9_out,
       and_10_out, and_11_out, and_12_out, and_13_out, and_14_out, and_15_out, and_16_out, and_17_out,
       and_18_out, n1bitadder_1_answer, not_1_out, not_2_out, not_3_out, not_4_out, not_5_out, not_6_out,
       not_7_out, not_8_out, not_9_out, not_10_out, not_11_out, not_12_out, not_13_out, not_14_out,
       not_15_out, or_1_out, xor_1_out, xor_2_out;

  not not_1 (not_1_out, S2);
  not not_2 (not_2_out, S1);
  and and_1 (and_1_out, not_1_out, not_2_out, not_3_out);
  not not_3 (not_3_out, S0);
  not not_4 (not_4_out, S2);
  and and_2 (and_2_out, not_4_out, not_5_out, S0);
  not not_5 (not_5_out, S1);
  not not_6 (not_6_out, S2);
  and and_3 (and_3_out, not_6_out, S1, not_7_out);
  not not_7 (not_7_out, S0);
  not not_8 (not_8_out, S2);
  and and_4 (and_4_out, not_8_out, S1, S0);
  not not_9 (not_9_out, S1);
  and and_5 (and_5_out, S2, not_9_out, not_10_out);
  not not_10 (not_10_out, S0);
  not not_11 (not_11_out, S1);
  and and_6 (and_6_out, S2, not_11_out, S0);
  and and_7 (and_7_out, S2, S1, not_12_out);
  not not_12 (not_12_out, S0);
  and and_8 (and_8_out, S2, S1, S0);
  not not_13 (not_13_out, A);
  _1BitAdder u_1bitadder_1 (.A_in(A), .B_in(B), .Carry_In(in_3), .Answer(n1bitadder_1_answer));  // open: Carry_Out
  xor xor_1 (xor_1_out, A, B);
  and and_9 (and_9_out, A, B);
  or or_1 (or_1_out, A, B);
  xor xor_2 (xor_2_out, A, B);
  and and_10 (and_10_out, not_13_out, A);
  and and_11 (and_11_out, and_1_out, n1bitadder_1_answer);
  and and_12 (and_12_out, and_2_out, xor_1_out);
  and and_13 (and_13_out, and_3_out, A);
  and and_14 (and_14_out, and_4_out, and_9_out);
  and and_15 (and_15_out, and_5_out, or_1_out);
  and and_16 (and_16_out, and_6_out, not_14_out);
  not not_14 (not_14_out, A);
  and and_17 (and_17_out, and_7_out, not_15_out);
  not not_15 (not_15_out, xor_2_out);
  and and_18 (and_18_out, and_8_out, and_10_out);
  or or_2 (out_7, and_11_out, and_12_out, and_13_out, and_14_out, and_15_out, and_16_out, and_17_out, and_18_out);

  // Notes on the sheet:
  //   Adam Yost
endmodule

// Adder
module _1BitAdder (
  input  A_in,
  input  B_in,
  input  Carry_In,
  output Answer,
  output Carry_Out
);

  wire and_1_out, and_2_out, xor_1_out;

  xor xor_1 (xor_1_out, A_in, B_in);
  xor xor_2 (Answer, xor_1_out, Carry_In);
  and and_1 (and_1_out, Carry_In, xor_1_out);
  and and_2 (and_2_out, B_in, A_in);
  or or_1 (Carry_Out, and_1_out, and_2_out);

  // Notes on the sheet:
  //   1 Bit Adder
  //   Adam Yost
endmodule

// Adder
module _4bitAdder (
  input  Carry_In,
  input  [3:0] A_in,
  input  [3:0] B_in,
  output [3:0] Output,
  output Carry_Out
);

  wire n1bitadder_1_carry_out, n1bitadder_2_carry_out, n1bitadder_3_carry_out;

  _1BitAdder u_1bitadder_1 (
    .A_in(A_in[0]), .B_in(B_in[0]), .Carry_In(Carry_In), .Answer(Output[0]),
    .Carry_Out(n1bitadder_1_carry_out));
  _1BitAdder u_1bitadder_2 (
    .A_in(A_in[1]), .B_in(B_in[1]), .Carry_In(n1bitadder_1_carry_out), .Answer(Output[1]),
    .Carry_Out(n1bitadder_2_carry_out));
  _1BitAdder u_1bitadder_3 (
    .A_in(A_in[2]), .B_in(B_in[2]), .Carry_In(n1bitadder_2_carry_out), .Answer(Output[2]),
    .Carry_Out(n1bitadder_3_carry_out));
  _1BitAdder u_1bitadder_4 (
    .A_in(A_in[3]), .B_in(B_in[3]), .Carry_In(n1bitadder_3_carry_out), .Answer(Output[3]),
    .Carry_Out(Carry_Out));
endmodule

module Split (
  input  In,
  output [3:0] out
);


  assign out = {4{In}};
endmodule

// Negation
module _4BitNegation (
  input  [3:0] A_in,
  output [3:0] Alternate_in
);

  Subtractor subtractor_1 (.B_in(A_in), .A_in(4'b0000), .Out(Alternate_in));

  // Notes on the sheet:
  //   0 - number
  //   Adam Yost
  //   Flips sign
endmodule

module Subtractor (
  input  [3:0] B_in,
  input  [3:0] A_in,
  output [3:0] Out
);

  wire [3:0] n4bitadder_1_output, not_1_out;

  _4bitAdder u_4bitadder_1 (
    .Carry_In(1'b0), .A_in(not_1_out), .B_in(A_in), .Output(n4bitadder_1_output));  // open: Carry_Out
  assign not_1_out = ~B_in;  // NOT_Gate not_1, 4 bits wide
  _4bitAdder u_4bitadder_2 (
    .Carry_In(1'b0), .A_in(n4bitadder_1_output), .B_in(4'b0001), .Output(Out));  // open: Carry_Out

  // Notes on the sheet:
  //   A - B
  //   Subtractor
  //   Adam Yost
endmodule

module Comparator (
  input  [3:0] in_1,
  input  [3:0] in_2,
  output [3:0] out_3
);

  wire not_1_out, not_2_out, not_3_out, not_4_out, xor_1_out, xor_2_out, xor_3_out, xor_4_out;

  xor xor_1 (xor_1_out, in_1[3], in_2[3]);
  not not_1 (not_1_out, xor_1_out);
  xor xor_2 (xor_2_out, in_1[2], in_2[2]);
  not not_2 (not_2_out, xor_2_out);
  xor xor_3 (xor_3_out, in_1[1], in_2[1]);
  not not_3 (not_3_out, xor_3_out);
  xor xor_4 (xor_4_out, in_1[0], in_2[0]);
  not not_4 (not_4_out, xor_4_out);
  and and_1 (out_3[0], not_4_out, not_3_out, not_2_out, not_1_out);

  assign out_3[3:1] = 3'b000;
endmodule

// Shift
module LeftShifter (
  input  [3:0] in_1,
  output [3:0] out_2
);


  assign out_2 = {in_1[2:0], 1'b0};
endmodule
