// Logisim project hw4part1.circ as structural Verilog: 2 circuits, main circuit main circuit
module main_circuit (
  input  A,
  input  B,
  input  C
);

  wire clock_1_out, RESET_out, statemachine_1_g, statemachine_1_r, statemachine_1_ready, statemachine_1_y;

  Clock clock_1 (.out(clock_1_out));
  statemachine statemachine_1 (
    .A(A), .B(B), .C(C), .CLK(clock_1_out), .RES(RESET_out), .R(statemachine_1_r), .Y(statemachine_1_y),
    .G(statemachine_1_g), .READY(statemachine_1_ready));
  Button RESET (.out(RESET_out));
  LED R (.in(statemachine_1_r));
  LED Y (.in(statemachine_1_y));
  LED G (.in(statemachine_1_g));
  LED READY (.in(statemachine_1_ready));

  // Notes on the sheet:
  //   Adam Yost
  //   Press Reset to Start
  //   Press the Reset button at any time to restart the state machine.
endmodule

module statemachine (
  input  A,
  input  B,
  input  C,
  input  CLK,
  input  RES,
  output R,
  output Y,
  output G,
  output READY
);

  wire and_1_out, and_2_out, and_3_out, and_4_out, and_5_out, and_6_out, and_7_out, and_8_out, and_9_out,
       and_10_out, and_11_out, in_0, in_1, in_2, in_3, in_4, in_5, nostate, not_1_out, not_2_out, not_3_out,
       not_4_out, not_5_out, not_6_out, or_1_out, or_4_out, or_6_out, or_7_out, out_1, out_2, out_3, out_5;

  not not_1 (not_1_out, A);
  not not_2 (not_2_out, B);
  not not_3 (not_3_out, C);
  and and_1 (and_1_out, A, READY);
  or or_1 (or_1_out, A, not_4_out);
  not not_4 (not_4_out, C);
  and and_2 (and_2_out, out_1, C);
  and and_3 (and_3_out, READY, B);
  not not_5 (not_5_out, C);
  and and_4 (and_4_out, out_2, C);
  and and_5 (and_5_out, READY, C);
  and and_6 (and_6_out, not_1_out, not_2_out, not_3_out);
  and and_7 (and_7_out, and_6_out, READY);
  or or_2 (in_0, and_7_out, nostate);
  or or_3 (in_1, and_1_out, and_8_out);
  and and_8 (and_8_out, out_1, or_1_out);
  or or_4 (or_4_out, and_2_out, and_3_out);
  or or_5 (in_2, or_4_out, and_9_out);
  and and_9 (and_9_out, out_2, or_6_out);
  or or_6 (or_6_out, B, not_5_out);
  or or_7 (or_7_out, and_4_out, and_5_out);
  or or_8 (in_3, or_7_out, and_10_out);
  and and_10 (and_10_out, out_3, C);
  not not_6 (not_6_out, C);
  and and_11 (and_11_out, not_6_out, out_3);
  or or_9 (in_4, and_11_out, out_5);
  Register #(.width(6)) register_1 (
    .D({in_5, in_4, in_3, in_2, in_1, in_0}), .Q({out_5, in_5, out_3, out_2, out_1, READY}), .clk(CLK),
    .clr(RES));  // open: en
  nor nor_1 (nostate, READY, out_1, out_2, out_3, in_5, out_5);
  or or_10 (G, out_1, out_2, in_5);
  or or_11 (Y, out_2, out_3, in_5);
  or or_12 (R, out_3, in_5);

  // Other names for the same wires on the sheet: out_0 = READY; out_4 = in_5

  // Notes on the sheet:
  //   Inputs
  //   Note: Do not move the input/output pins.  Do not add any additional inputs/outputs.
  //   CLK is the clock input and should be wired to the clock input of the register
  //   RES is the reset signal and should be wired to the '0' input of the register
  //   Build your state machine using onehot in this subcircuit
  //   Adam Yost
  //   Outputs
endmodule
