// Logisim project hw4part2.circ as structural Verilog: 1 circuit, main circuit my circuit
module my_circuit (
  input  A,
  output X,
  output Y,
  output Z
);

  wire and_1_out, and_2_out, and_3_out, and_4_out, and_5_out, and_6_out, and_7_out, and_8_out, and_9_out,
       and_10_out, and_11_out, and_12_out, and_13_out, and_14_out, and_15_out, and_16_out, and_17_out,
       and_18_out, CLK, in_0, in_1, in_2, not_1_out, not_2_out, not_3_out, not_4_out, not_5_out, not_6_out,
       not_7_out, not_8_out, not_9_out, not_10_out, not_11_out, not_12_out, not_13_out, not_14_out,
       not_15_out, not_16_out, not_17_out, not_18_out, not_19_out, not_20_out, not_21_out, not_22_out,
       not_23_out, out_0, out_1, out_2, RES;

  Clock clock_1 (.out(CLK));
  Button button_1 (.out(RES));
  Register #(.width(3)) register_1 (
    .D({in_0, in_1, in_2}), .Q({out_0, out_1, out_2}), .clk(CLK), .clr(RES));  // open: en
  not not_1 (not_1_out, A);
  and and_1 (and_1_out, not_1_out, not_2_out, out_2);
  not not_2 (not_2_out, out_0);
  not not_3 (not_3_out, A);
  and and_2 (and_2_out, not_3_out, out_0, out_1);
  and and_3 (and_3_out, A, out_0, not_4_out);
  not not_4 (not_4_out, out_1);
  and and_4 (and_4_out, A, not_5_out, not_6_out);
  not not_5 (not_5_out, out_2);
  not not_6 (not_6_out, out_1);
  and and_5 (and_5_out, out_0, not_7_out);
  not not_7 (not_7_out, out_2);
  not not_8 (not_8_out, out_0);
  not not_9 (not_9_out, out_1);
  not not_10 (not_10_out, A);
  not not_11 (not_11_out, A);
  not not_12 (not_12_out, out_2);
  not not_13 (not_13_out, out_2);
  or or_1 (in_2, and_1_out, and_2_out, and_3_out, and_4_out, and_5_out);
  and and_6 (and_6_out, not_8_out, not_9_out, out_2);
  and and_7 (and_7_out, not_10_out, out_1, out_2);
  or or_2 (in_1, and_6_out, and_7_out, and_8_out, and_9_out);
  and and_8 (and_8_out, not_11_out, out_0, not_12_out);
  and and_9 (and_9_out, A, out_1, not_13_out);
  not not_14 (not_14_out, out_0);
  and and_10 (and_10_out, A, not_14_out, out_1, out_2);
  not not_15 (not_15_out, A);
  and and_11 (and_11_out, not_15_out, out_1, not_16_out);
  not not_16 (not_16_out, out_2);
  not not_17 (not_17_out, A);
  and and_12 (and_12_out, not_17_out, out_0, out_1);
  and and_13 (and_13_out, A, out_0, not_18_out);
  not not_18 (not_18_out, out_1);
  and and_14 (and_14_out, out_0, not_19_out);
  not not_19 (not_19_out, out_2);
  or or_3 (in_0, and_10_out, and_11_out, and_12_out, and_13_out, and_14_out);
  not not_20 (not_20_out, out_1);
  and and_15 (and_15_out, not_20_out, out_2);
  and and_16 (and_16_out, out_1, not_21_out);
  not not_21 (not_21_out, out_2);
  not not_22 (not_22_out, out_1);
  or or_4 (Y, not_22_out, out_0);
  and and_17 (and_17_out, out_1, out_2);
  not not_23 (not_23_out, out_0);
  and and_18 (and_18_out, not_23_out, out_2);
  or or_5 (X, and_15_out, and_16_out);
  or or_6 (Z, and_17_out, and_18_out);

  // Notes on the sheet:
  //   Adam Yost
endmodule
