// Logisim project lab8part2.circ as structural Verilog: 1 circuit, main circuit my circuit
module my_circuit (
  input  in_1,
  input  in_2,
  input  in_3
);

  wire and_1_out, and_2_out, and_3_out, and_4_out, and_5_out, and_6_out, and_7_out, and_8_out, and_9_out,
       and_10_out, and_11_out, and_12_out, and_13_out, and_15_out, and_16_out, CLK, G, in_0, in_1_t, in_2_t,
       in_3_t, in_4, in_5, in_6, in_7, in_8, nor_1_out, nor_2_out, nostate, or_2_out, or_3_out, or_5_out,
       or_6_out, out_0, out_1, out_2, out_3, out_4, out_6, out_7, out_8, P, R, RES, Y;

  and and_1 (and_1_out, out_2, in_2);
  and and_2 (and_2_out, out_1, in_2);
  and and_3 (and_3_out, out_3, in_1);
  and and_4 (and_4_out, out_1, in_1);
  Button button_1 (.out(P));
  nor nor_1 (nor_1_out, in_1, in_2, in_3, P);
  and and_5 (and_5_out, out_0, P);
  and and_6 (and_6_out, out_1, nor_2_out);
  nor nor_2 (nor_2_out, in_1, in_2, in_3);
  and and_7 (and_7_out, in_3, out_1);
  or or_1 (in_2_t, and_7_out, and_8_out);
  and and_8 (and_8_out, out_2, or_2_out);
  or or_2 (or_2_out, in_3, ~in_2);  // OR_Gate
  or or_3 (or_3_out, and_1_out, and_2_out);
  or or_4 (in_3_t, or_3_out, and_9_out);
  and and_9 (and_9_out, out_3, or_5_out);
  or or_5 (or_5_out, in_2, ~in_1);  // OR_Gate
  or or_6 (or_6_out, and_3_out, and_4_out);
  or or_7 (in_4, or_6_out, and_10_out);
  and and_10 (and_10_out, out_4, in_1);
  Clock clock_1 (.out(CLK));
  Button button_2 (.out(RES));
  and and_11 (and_11_out, nor_1_out, out_0);
  or or_8 (in_0, and_11_out, nostate);
  or or_9 (in_1_t, and_5_out, and_6_out);
  and and_12 (and_12_out, ~in_1, out_4);  // AND_Gate
  and and_13 (and_13_out, out_6, ~P);  // AND_Gate
  and and_14 (in_7, out_6, P);
  and and_15 (and_15_out, out_8, ~P);  // AND_Gate
  and and_16 (and_16_out, out_8, P);
  or or_10 (in_5, and_12_out, and_16_out, and_13_out);
  or or_11 (in_8, and_15_out, out_7);
  Register #(.width(9)) register_1 (
    .D({in_8, in_7, in_6, in_5, in_4, in_3_t, in_2_t, in_1_t, in_0}),
    .Q({out_8, out_7, out_6, in_6, out_4, out_3, out_2, out_1, out_0}), .clk(CLK), .clr(RES));  // open: en
  nor nor_3 (nostate, out_0, out_1, out_2, out_3, out_4, in_6, out_6, out_7, out_8);
  LED u_G (.in(G));
  LED u_R (.in(R));
  LED u_Y (.in(Y));
  LED READY (.in(out_1));
  or or_12 (R, out_4, out_6);
  or or_13 (G, out_2, out_6);
  or or_14 (Y, out_3, out_6);

  // Other names for the same wires on the sheet: out_5 = in_6; READY = out_1; A = in_1; B = in_2; C = in_3
endmodule
