// Logisim project lab8part3.circ as structural Verilog: 1 circuit, main circuit my circuit
module my_circuit (
  input  in_1,
  input  in_2,
  input  in_3,
  input  in_4
);

  wire and_1_out, and_2_out, and_3_out, and_4_out, and_5_out, and_6_out, CLK, in_0, in_1_t, in_2_t, in_3_t,
       nostate, or_1_out, or_2_out, or_4_out, or_7_out, out_0, out_1, out_2, out_3;

  or or_1 (or_1_out, out_1, out_2, out_3);
  and and_1 (and_1_out, or_1_out, in_3);
  or or_2 (or_2_out, out_0, out_2, out_3);
  and and_2 (and_2_out, ~in_1, ~in_2, out_0);  // AND_Gate
  and and_3 (and_3_out, or_2_out, in_1);
  or or_3 (in_1_t, and_3_out, and_4_out);
  and and_4 (and_4_out, ~in_2, ~in_3, out_1);  // AND_Gate
  or or_4 (or_4_out, out_0, out_1);
  and and_5 (and_5_out, or_4_out, in_2);
  and and_6 (and_6_out, out_3, ~in_1, ~in_3);  // AND_Gate
  and and_7 (in_3_t, out_2, ~in_1, ~in_3);  // AND_Gate
  or or_5 (in_0, and_2_out, and_1_out, nostate);
  or or_6 (in_2_t, and_5_out, and_6_out);
  Clock clock_1 (.out(CLK));
  or or_7 (or_7_out, out_1, out_3);
  Register #(.width(4)) register_1 (
    .D({in_3_t, in_2_t, in_1_t, in_0}), .Q({out_3, out_2, out_1, out_0}), .clk(CLK), .clr(in_4));  // open: en
  LED led_1 (.in(or_7_out));
  nor nor_1 (nostate, out_0, out_1, out_2, out_3);

  // Other names for the same wires on the sheet: A = in_1; B = in_2; C = in_3; RES = in_4
endmodule
