// Logisim project tl1.circ as structural Verilog: 3 circuits, main circuit truth tables
module truth_tables (
  input  A,
  input  B,
  input  C,
  output X
);

  wire and_1_out, and_2_out, and_3_out, and_4_out, not_1_out, not_2_out, not_3_out, not_4_out, not_5_out,
       not_6_out, not_7_out;

  not not_1 (not_1_out, A);
  not not_2 (not_2_out, B);
  and and_1 (and_1_out, not_1_out, not_2_out, not_3_out);
  not not_3 (not_3_out, C);
  not not_4 (not_4_out, A);
  and and_2 (and_2_out, not_4_out, not_5_out, C);
  not not_5 (not_5_out, B);
  not not_6 (not_6_out, A);
  and and_3 (and_3_out, not_6_out, B, C);
  and and_4 (and_4_out, A, B, not_7_out);
  not not_7 (not_7_out, C);
  or or_1 (X, and_1_out, and_2_out, and_3_out, and_4_out);

  // Notes on the sheet:
  //   Adam Yost
endmodule

module _4_bit_MUX (
  input  A,
  input  B,
  input  [3:0] in_0,
  input  [3:0] in_1,
  input  [3:0] in_2,
  input  [3:0] in_3,
  output [3:0] out
);

  wire not_1_out, not_2_out, not_3_out, not_4_out;
  wire [3:0] and_5_out, and_6_out, and_7_out, and_8_out;
  wire [3:3] and_1_out, and_2_out, and_3_out, and_4_out;

  not not_1 (not_1_out, A);
  not not_2 (not_2_out, B);
  not not_3 (not_3_out, A);
  and and_1 (and_1_out[3], A, not_4_out);
  not not_4 (not_4_out, B);
  and and_2 (and_2_out[3], A, B);
  and and_3 (and_3_out[3], not_1_out, not_2_out);
  and and_4 (and_4_out[3], not_3_out, B);
  assign and_5_out = {4{and_3_out[3]}} & in_0;  // AND_Gate and_5, 4 bits wide
  assign and_6_out = {4{and_4_out[3]}} & in_1;  // AND_Gate and_6, 4 bits wide
  assign and_7_out = {4{and_1_out[3]}} & in_2;  // AND_Gate and_7, 4 bits wide
  assign and_8_out = {4{and_2_out[3]}} & in_3;  // AND_Gate and_8, 4 bits wide
  assign out = and_5_out | and_6_out | and_7_out | and_8_out;  // OR_Gate or_1, 4 bits wide

  // Notes on the sheet:
  //   Adam Yost
endmodule

module Transistor_time (
  input  A,
  input  B,
  input  C,
  input  D,
  output out
);

  wire transistor_1_out, transistor_3_out, transistor_5_out, transistor_7_out, transistor_9_out,
       transistor_11_out, transistor_13_out, transistor_15_out, transistor_17_out, transistor_19_out;

  Transistor transistor_1 (.in(1'b1), .out(transistor_1_out), .gate(B));
  Transistor #(.\type ("n")) transistor_2 (.in(1'b0), .out(transistor_1_out), .gate(B));
  Transistor transistor_3 (.in(1'b1), .out(transistor_3_out), .gate(C));
  Transistor #(.\type ("n")) transistor_4 (.in(1'b0), .out(transistor_3_out), .gate(C));
  Transistor transistor_5 (.in(1'b1), .out(transistor_5_out), .gate(A));
  Transistor #(.\type ("n")) transistor_6 (.in(transistor_7_out), .out(transistor_5_out), .gate(transistor_1_out));
  Transistor #(.\type ("n")) transistor_7 (.in(1'b0), .out(transistor_7_out), .gate(A));
  Transistor transistor_8 (.in(1'b1), .out(transistor_5_out), .gate(transistor_1_out));
  Transistor transistor_9 (.in(1'b1), .out(transistor_9_out), .gate(transistor_5_out));
  Transistor #(.\type ("n")) transistor_10 (.in(1'b0), .out(transistor_9_out), .gate(transistor_5_out));
  Transistor transistor_11 (.in(1'b1), .out(transistor_11_out), .gate(transistor_9_out));
  Transistor #(.\type ("n")) transistor_12 (.in(transistor_13_out), .out(transistor_11_out), .gate(transistor_3_out));
  Transistor #(.\type ("n")) transistor_13 (.in(1'b0), .out(transistor_13_out), .gate(transistor_9_out));
  Transistor transistor_14 (.in(1'b1), .out(transistor_11_out), .gate(transistor_3_out));
  Transistor transistor_15 (.in(1'b1), .out(transistor_15_out), .gate(transistor_11_out));
  Transistor #(.\type ("n")) transistor_16 (.in(1'b0), .out(transistor_15_out), .gate(transistor_11_out));
  Transistor transistor_17 (.in(1'b1), .out(transistor_17_out), .gate(transistor_15_out));
  Transistor #(.\type ("n")) transistor_18 (.in(transistor_19_out), .out(transistor_17_out), .gate(D));
  Transistor #(.\type ("n")) transistor_19 (.in(1'b0), .out(transistor_19_out), .gate(transistor_15_out));
  Transistor transistor_20 (.in(1'b1), .out(transistor_17_out), .gate(D));
  Transistor transistor_21 (.in(1'b1), .out(out), .gate(transistor_17_out));
  Transistor #(.\type ("n")) transistor_22 (.in(1'b0), .out(out), .gate(transistor_17_out));

  // Notes on the sheet:
  //   A & !B & !C & D
  //   Adam Yost
endmodule
