// Logisim project tl2.circ as structural Verilog: 3 circuits, main circuit main circuit
module main_circuit (
  input  A
);

  wire clock_1_out, RES_out, state_machine_1_w, state_machine_1_x, state_machine_1_y, state_machine_1_z;

  Clock clock_1 (.out(clock_1_out));
  Button RES (.out(RES_out));
  State_Machine state_machine_1 (
    .A(A), .CLK(clock_1_out), .RES(RES_out), .W(state_machine_1_w), .X(state_machine_1_x),
    .Y(state_machine_1_y), .Z(state_machine_1_z));
  LED W (.in(state_machine_1_w));
  LED X (.in(state_machine_1_x));
  LED Y (.in(state_machine_1_y));
  LED Z (.in(state_machine_1_z));

  // Notes on the sheet:
  //   My name is
  //   Adam Yost
  //   and this is my pretty state machine!
endmodule

module Register (
  input  [7:0] D,
  input  CLK,
  input  RES,
  input  EN,
  output [7:0] Q
);

  D_Flip_Flop d_ff_1 (.clk(CLK), .D(D[0]), .Q(Q[0]), .en(EN), .reset(RES));  // open: Qn, preset
  D_Flip_Flop d_ff_2 (.clk(CLK), .D(D[1]), .Q(Q[1]), .en(EN), .reset(RES));  // open: Qn, preset
  D_Flip_Flop d_ff_3 (.clk(CLK), .D(D[2]), .Q(Q[2]), .en(EN), .reset(RES));  // open: Qn, preset
  D_Flip_Flop d_ff_4 (.clk(CLK), .D(D[3]), .Q(Q[3]), .en(EN), .reset(RES));  // open: Qn, preset
  D_Flip_Flop d_ff_5 (.clk(CLK), .D(D[4]), .Q(Q[4]), .en(EN), .reset(RES));  // open: Qn, preset
  D_Flip_Flop d_ff_6 (.clk(CLK), .D(D[5]), .Q(Q[5]), .en(EN), .reset(RES));  // open: Qn, preset
  D_Flip_Flop d_ff_7 (.clk(CLK), .D(D[6]), .Q(Q[6]), .en(EN), .reset(RES));  // open: Qn, preset
  D_Flip_Flop d_ff_8 (.clk(CLK), .D(D[7]), .Q(Q[7]), .en(EN), .reset(RES));  // open: Qn, preset

  // Notes on the sheet:
  //   8 Bit Register
endmodule

module State_Machine (
  input  A,
  input  CLK,
  input  RES,
  output W,
  output X,
  output Y,
  output Z
);

  wire and_1_out, and_2_out, and_3_out, and_4_out, and_5_out, and_6_out, and_7_out, and_8_out, in_0, in_1,
       in_2, out_0, out_1, out_2;

  and and_1 (and_1_out, ~out_2, ~out_1, ~A);  // AND_Gate
  or or_1 (in_2, and_1_out, and_2_out);
  and and_2 (and_2_out, A, ~out_2, out_1, out_0);  // AND_Gate
  and and_3 (and_3_out, A, ~out_2, ~out_1, out_0);  // AND_Gate
  and and_4 (and_4_out, A, ~out_2, out_1, ~out_0);  // AND_Gate
  and and_5 (and_5_out, ~A, out_2);  // AND_Gate
  and and_6 (and_6_out, ~A, out_1, out_0);  // AND_Gate
  or or_2 (in_1, and_5_out, and_6_out, and_3_out, and_4_out);
  and and_7 (and_7_out, A, ~out_1, ~out_0);  // AND_Gate
  and and_8 (and_8_out, out_1, ~out_0);  // AND_Gate
  Register_part #(.width(3)) register_1 (
    .D({in_0, in_1, in_2}), .Q({out_0, out_1, out_2}), .clk(CLK), .clr(RES));  // open: en
  or or_3 (in_0, and_7_out, out_2, and_8_out);
  and and_9 (W, ~out_2, ~out_1, out_0);  // AND_Gate
  and and_10 (X, ~out_2, out_1, ~out_0);  // AND_Gate
  and and_11 (Y, ~out_2, out_1, out_0);  // AND_Gate
  and and_12 (Z, out_2, ~out_1, ~out_0);  // AND_Gate
endmodule
